# Fritzing sketch Photoflux (saved by Fritzing 0.9.10b)
breadboards: 1

parts:
  R1 = PHOTOCELL [package=photocell-kit]  # not connected
  LED1 = smd LED [color="Red (633nm)" package="1206 [SMD]"]  # not connected
  A1 = Arduino UNO R4 WiFi
  VCC1 = Battery block 9V
  Mod1 = KY-019 5V Relay Module [package="Breakout board"]
  S1 = Taiway 100-SP-X-T1 SPDT Miniature Toggle Switch [part_number=100-SP-X-T1-0-0-B1-M2 package=THT]

nets:
  N1: A1.Pin_10, VCC1.-
  N2: A1.Pin_11, VCC1.+, S1.L2
  N3: Mod1.NC, S1.L1

custom parts:
  Arduino UNO R4 WiFi: The Arduino UNO R4 WiFi merges the RA4M1 microprocessor from Renesas with the ESP32-S3 from Espressif, creating an all-in-one tool for makers with enhanced processing power and a diverse array of new peripherals.
  KY-019 5V Relay Module: KY-019 5V Relay module, used to control AC circuits. (Special thanks to vanepp for fixing the PCB holes and other errors)
